# Fritzing sketch coeur led2 (saved by Fritzing 0.9.3b)
breadboards: 1

parts:
  Composant1 = Arduino Uno (Rev3)
  LED1 = LED - 3mm [color="Red (633nm)" package="3 mm [THT]"]
  LED3 = LED - 3mm [color="Red (633nm)" package="3 mm [THT]"]
  LED4 = LED - 3mm [color="Red (633nm)" package="3 mm [THT]"]
  LED5 = LED - 3mm [color="Red (633nm)" package="3 mm [THT]"]
  LED6 = LED - 3mm [color="Red (633nm)" package="3 mm [THT]"]
  LED7 = LED - 3mm [color="Red (633nm)" package="3 mm [THT]"]
  LED8 = LED - 3mm [color="Red (633nm)" package="3 mm [THT]"]
  LED9 = LED - 3mm [color="Red (633nm)" package="3 mm [THT]"]
  LED10 = LED - 3mm [color="Red (633nm)" package="3 mm [THT]"]
  R1 = Resistor [tolerance=±5% resistance=220 package="0402 [SMD]"]
  R2 = Resistor [tolerance=±5% resistance=220 package="0402 [SMD]"]
  R3 = Resistor [tolerance=±5% resistance=220 package="0402 [SMD]"]
  R4 = Resistor [tolerance=±5% resistance=220 package="0402 [SMD]"]
  R5 = Resistor [tolerance=±5% resistance=220 package="0402 [SMD]"]
  R6 = Resistor [tolerance=±5% resistance=220 package="0402 [SMD]"]
  R7 = Resistor [tolerance=±5% resistance=220 package="0402 [SMD]"]
  R8 = Resistor [tolerance=±5% resistance=220 package="0402 [SMD]"]
  R9 = Resistor [tolerance=±5% resistance=220 package="0402 [SMD]"]
  R10 = Resistor [tolerance=±5% resistance=220 package="0402 [SMD]"]
  LED11 = LED - 3mm [color="Red (633nm)" package="3 mm [THT]"]

nets:
  N1: Composant1.D8, LED7.cathode
  N2: Composant1.D9_PWM, LED8.cathode
  N3: Composant1.D10_PWM/SS, LED9.cathode
  N4: Composant1.D11_PWM/MOSI, LED10.cathode
  N5: Composant1.GND, R1.Pin_0, R2.Pin_0, R3.Pin_0, R4.Pin_0, R5.Pin_0, R6.Pin_0, R7.Pin_0, R8.Pin_0, R9.Pin_0, R10.Pin_0
  N6: Composant1.D2, LED1.cathode
  N7: Composant1.D3_PWM, LED11.cathode
  N8: Composant1.D4, LED3.cathode
  N9: Composant1.D5_PWM, LED4.cathode
  N10: Composant1.D6_PWM, LED5.cathode
  N11: Composant1.D7, LED6.cathode
  N12: LED1.anode, R1.Pin_1
  N13: LED3.anode, R3.Pin_1
  N14: LED4.anode, R4.Pin_1
  N15: LED5.anode, R5.Pin_1
  N16: LED6.anode, R6.Pin_1
  N17: LED7.anode, R7.Pin_1
  N18: LED8.anode, R8.Pin_1
  N19: LED9.anode, R9.Pin_1
  N20: LED10.anode, R10.Pin_1
  N21: R2.Pin_1, LED11.anode
